# Fritzing sketch AAC_board (saved by Fritzing 0.9.9b)
breadboards: 1

parts:
  Part1 = Adafruit Feather RP2040 [part_number="Adafruit #4884"]
  Part2 = AirLift FeatherWing  # not connected
  Part3 = Adafruit STEMMA Speaker [part_number="Adafruit #3885"]
  Part4 = Adafruit MPR121 [part_number="Adafruit #1982"]
  S1 = Pushbutton [package="[THT]"]
  R1 = Resistor [tolerance=±5% power=0.25 resistance=10000 package=THT]

nets:
  GND: Part1.GND, Part1.D5, Part3.GND, Part4.GND, S1.Pin_1, S1.Pin_2
  +3V3: Part1.+3V3, Part3.VDD, Part4.VCC, R1.Pin_0
  N1: Part1.SDA, Part4.SDA
  N2: Part1.SCL, Part4.SCL
  N3: Part1.A0, Part3.SIG
  N4: Part1.D6, S1.Pin_3, S1.Pin_4, R1.Pin_1

custom parts:
  Adafruit Feather RP2040: A new chip means a new Feather, and the Raspberry Pi RP2040 is no exception. When we saw this chip we thought "this chip is going to be awesome when we give it the Feather Treatment" and so we did! This Feather features the RP2040, and all niceties you know and love about Feather Measures 2.0" x 0.9" x 0.28" (50.8mm x 22.8mm x 7mm) without headers soldered in Light as a (large?) feather - 5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
  AirLift FeatherWing: Give your Feather project a lift with the Adafruit AirLift FeatherWing - a FeatherWing that lets you use the powerful ESP32 as a WiFi co-processor. You probably have your favorite Feather (like the Feather M4) that comes with its own set of awesome peripherals and lots of libraries. But it doesn't have WiFi built in! So lets give that chip a best friend, the ESP32. This chip can handle all the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
  Adafruit STEMMA Speaker: Hey, have you heard the good news? With Adafruit STEMMA boards you can easily and safely plug sensors and devices together, like this Adafruit STEMMA Speaker - Plug and Play Audio Amplifier. Like the name implies, it's got a class D audio amplifier on board, and our favorite little 1 Watt 8 ohm speaker. Connecting it up is easy - you only need ground, 3 to 5V power, and audio signal. The audio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
  Adafruit MPR121: Add lots of touch sensors to your next microcontroller project with this easy-to-use 12-channel capacitive touch sensor breakout board, starring the MPR121. This chip can handle up to 12 individual touch pads. The MPR121 has support for only I2C, which can be implemented with nearly any microcontroller. You can select one of 4 addresses with the ADDR pin, for a total of 48 capacitive touch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
